// Logisim project Cpu.circ as structural Verilog
module main (
  input  in_1,
  input  [3:0] in_2,
  input  in_3,
  input  [3:0] in_4,
  input  [15:0] in_5,
  input  [15:0] in_6,
  input  [4:0] in_7,
  output [15:0] out_8,
  output JMP
);

  wire clk_out, decoder_1_out0, decoder_1_out1, decoder_1_out2, decoder_1_out3, decoder_1_out4,
       decoder_1_out5, decoder_1_out6, decoder_1_out7, decoder_1_out8, decoder_1_out9, decoder_1_out10,
       decoder_1_out11, decoder_1_out12, decoder_1_out13, decoder_1_out14, decoder_1_out15, decoder_2_out0,
       decoder_2_out1, decoder_2_out2, decoder_2_out3, decoder_2_out4, decoder_2_out5, decoder_2_out6,
       decoder_2_out7, decoder_2_out8, decoder_2_out9, decoder_2_out10, decoder_2_out11, decoder_2_out12,
       decoder_2_out13, decoder_2_out14, decoder_2_out15, or_1_out, or_2_out, or_3_out, or_4_out, or_5_out,
       or_6_out, or_7_out, or_8_out, or_9_out, or_10_out, or_11_out, or_12_out, or_13_out, or_14_out,
       or_15_out, or_16_out, undriven;
  wire [15:0] adder_1_out, and_1_out, divider_1_out, multiplier_1_out, not_1_out, or_17_out, or_18_out,
       shifter_1_out, shifter_2_out, subtractor_1_out;

  Decoder #(.select(4)) decoder_1 (
    .out0(decoder_1_out0), .out1(decoder_1_out1), .out2(decoder_1_out2), .out3(decoder_1_out3),
    .out4(decoder_1_out4), .out5(decoder_1_out5), .out6(decoder_1_out6), .out7(decoder_1_out7),
    .out8(decoder_1_out8), .out9(decoder_1_out9), .out10(decoder_1_out10), .out11(decoder_1_out11),
    .out12(decoder_1_out12), .out13(decoder_1_out13), .out14(decoder_1_out14), .out15(decoder_1_out15),
    .sel(in_2), .en(in_1));
  Decoder #(.select(4)) decoder_2 (
    .out0(decoder_2_out0), .out1(decoder_2_out1), .out2(decoder_2_out2), .out3(decoder_2_out3),
    .out4(decoder_2_out4), .out5(decoder_2_out5), .out6(decoder_2_out6), .out7(decoder_2_out7),
    .out8(decoder_2_out8), .out9(decoder_2_out9), .out10(decoder_2_out10), .out11(decoder_2_out11),
    .out12(decoder_2_out12), .out13(decoder_2_out13), .out14(decoder_2_out14), .out15(decoder_2_out15),
    .sel(in_4), .en(in_3));
  or or_1 (or_1_out, decoder_1_out0, decoder_2_out0);
  or or_2 (or_2_out, decoder_1_out1, decoder_2_out1);
  or or_3 (or_3_out, decoder_1_out2, decoder_2_out2);
  or or_4 (or_4_out, decoder_1_out3, decoder_2_out3);
  or or_5 (or_5_out, decoder_1_out4, decoder_2_out4);
  or or_6 (or_6_out, decoder_1_out5, decoder_2_out5);
  or or_7 (or_7_out, decoder_1_out10, decoder_2_out10);
  or or_8 (or_8_out, decoder_1_out11, decoder_2_out11);
  or or_9 (or_9_out, decoder_1_out12, decoder_2_out12);
  or or_10 (or_10_out, decoder_1_out13, decoder_2_out13);
  or or_11 (or_11_out, decoder_1_out14, decoder_2_out14);
  or or_12 (or_12_out, decoder_1_out15, decoder_2_out15);
  or or_13 (or_13_out, decoder_1_out6, decoder_2_out6);
  or or_14 (or_14_out, decoder_1_out7, decoder_2_out7);
  or or_15 (or_15_out, decoder_1_out8, decoder_2_out8);
  or or_16 (or_16_out, decoder_1_out9, decoder_2_out9);
  Clock clk (.out(clk_out));
  // RGB_Video #(.height(192), .scale(3), .width(256)) rgb_video_1: pin names not known
  registerwithreadenable r0 (
    .data_reg(out_8), .write_enable_reg(or_1_out), .clock_reg(clk_out), .read_enable_reg(undriven),
    .output_reg(out_8));
  registerwithreadenable r1 (
    .data_reg(out_8), .write_enable_reg(or_2_out), .clock_reg(clk_out), .output_reg(out_8));  // open: read_enable_reg
  registerwithreadenable r2 (
    .data_reg(out_8), .write_enable_reg(or_3_out), .clock_reg(clk_out), .output_reg(out_8));  // open: read_enable_reg
  registerwithreadenable r3 (
    .data_reg(out_8), .write_enable_reg(or_4_out), .clock_reg(clk_out), .output_reg(out_8));  // open: read_enable_reg
  registerwithreadenable r4 (
    .data_reg(out_8), .write_enable_reg(or_5_out), .clock_reg(clk_out), .output_reg(out_8));  // open: read_enable_reg
  registerwithreadenable r5 (
    .data_reg(out_8), .write_enable_reg(or_6_out), .clock_reg(clk_out), .output_reg(out_8));  // open: read_enable_reg
  registerwithreadenable r6 (
    .data_reg(out_8), .write_enable_reg(or_13_out), .clock_reg(clk_out), .output_reg(out_8));  // open: read_enable_reg
  registerwithreadenable r7 (
    .data_reg(out_8), .write_enable_reg(or_14_out), .clock_reg(clk_out), .output_reg(out_8));  // open: read_enable_reg
  registerwithreadenable r8 (
    .data_reg(out_8), .write_enable_reg(or_15_out), .clock_reg(clk_out), .output_reg(out_8));  // open: read_enable_reg
  registerwithreadenable r9 (
    .data_reg(out_8), .write_enable_reg(or_16_out), .clock_reg(clk_out), .output_reg(out_8));  // open: read_enable_reg
  registerwithreadenable r10 (
    .data_reg(out_8), .write_enable_reg(or_7_out), .clock_reg(clk_out), .output_reg(out_8));  // open: read_enable_reg
  registerwithreadenable r11 (
    .data_reg(out_8), .write_enable_reg(or_8_out), .clock_reg(clk_out), .output_reg(out_8));  // open: read_enable_reg
  Pull_Resistor pull_resistor_1 (.node(out_8));
  Register #(.width(1)) JZ (.clk(clk_out));  // open: D, en, Q, clr
  ROM #(.addrWidth(16), .dataWidth(16)) Program_memory ();  // open: addr, data
  registerwithreadenable Jump_target_reg_r12 (
    .data_reg(out_8), .write_enable_reg(or_9_out), .clock_reg(clk_out));  // open: read_enable_reg, output_reg
  Register #(.width(1)) JG ();  // open: D, en, clk, Q, clr
  registerwithreadenable accumulator_r13 (.write_enable_reg(or_10_out));  // open: data_reg, clock_reg, read_enable_reg, output_reg
  registerwithreadenable stack_ptr_r14 (
    .data_reg(out_8), .write_enable_reg(or_11_out), .clock_reg(clk_out));  // open: read_enable_reg, output_reg
  registerwithreadenable memory_address_register_r15 (
    .data_reg(out_8), .write_enable_reg(or_12_out), .clock_reg(clk_out));  // open: read_enable_reg, output_reg
  Register #(.width(1)) JS ();  // open: D, en, clk, Q, clr
  Register #(.width(1)) JO ();  // open: D, en, clk, Q, clr
  Register #(.width(1)) JV ();  // open: D, en, clk, Q, clr
  // DualRAM #(.addrWidth(16), .dataWidth(16)) data_memory: pin names not known
  Adder #(.width(16)) adder_1 (.out(adder_1_out));  // open: a, b, cin, cout
  Subtractor #(.width(16)) subtractor_1 (.out(subtractor_1_out));  // open: a, b, bin, bout
  Multiplier #(.mode("twosComplement"), .width(16)) multiplier_1 (.out(multiplier_1_out));  // open: a, b, cin, cout
  Divider #(.mode("twosComplement"), .width(16)) divider_1 (.out(divider_1_out));  // open: a, b, upper, rem
  // AND_Gate and_1 has open pins: out=and_1_out
  // OR_Gate or_17 has open pins: out=or_17_out
  // OR_Gate or_18 has open pins: out=or_18_out
  // NOT_Gate not_1 has open pins: in=open, out=not_1_out
  Shifter #(.width(16)) shifter_1 (.out(shifter_1_out));  // open: in, dist
  Shifter #(.shift("lr"), .width(16)) shifter_2 (.out(shifter_2_out));  // open: in, dist
  Comparator comparator_1 ();  // open: a, b, gt, eq, lt
  Multiplexer #(.select(5), .width(16)) multiplexer_1 (
    .in1(adder_1_out), .in2(subtractor_1_out), .in3(multiplier_1_out), .in4(divider_1_out), .in5(and_1_out),
    .in6(or_17_out), .in7(or_18_out), .in8(not_1_out), .in9(shifter_1_out), .in10(shifter_2_out), .sel(in_7));  // open: in0, in11, in12, in13, in14, in15, in16, in17, in18, in19, in20, in21, in22, in23, in24, in25, in26, in27, in28, in29, in30, in31, out

  assign JMP = 1'b1;

  // Notes on the sheet:
  //   Src1
  //   Src2
endmodule

module registerwithreadenable (
  input  [15:0] data_reg,
  input  write_enable_reg,
  input  clock_reg,
  input  read_enable_reg,
  output [15:0] output_reg
);

  wire [15:0] register_1_q;

  Register #(.width(16)) register_1 (
    .D(data_reg), .en(write_enable_reg), .clk(clock_reg), .Q(register_1_q));  // open: clr
  Multiplexer #(.width(16)) multiplexer_1 (.in1(register_1_q), .out(output_reg), .sel(read_enable_reg));  // open: in0
endmodule
